// Logisim project Calculator.circ as structural Verilog
module FullAdder (
  input  A,
  input  B,
  input  Cin,
  output Sum,
  output Cout
);

  wire and_1_out, and_2_out, xor_1_out;

  xor xor_1 (xor_1_out, A, B);
  xor xor_2 (Sum, xor_1_out, Cin);
  and and_1 (and_1_out, xor_1_out, Cin);
  and and_2 (and_2_out, A, B);
  or or_1 (Cout, and_1_out, and_2_out);
endmodule

module Adder8bit (
  input  in_1,
  input  in_2,
  input  in_3,
  input  in_4,
  input  in_5,
  input  in_6,
  input  in_7,
  input  in_8,
  input  in_9,
  input  in_10,
  input  in_11,
  input  in_12,
  input  in_13,
  input  in_14,
  input  in_15,
  input  in_16,
  input  Cin,
  output S0,
  output S1,
  output S2,
  output S3,
  output S4,
  output S5,
  output S6,
  output S7,
  output Cout
);

  wire FA0_cout, FA1_cout, FA2_cout, FA3_cout, FA4_cout, FA5_cout, FA6_cout;

  FullAdder FA0 (.A(in_2), .B(in_1), .Cin(Cin), .Sum(S0), .Cout(FA0_cout));
  FullAdder FA1 (.A(in_4), .B(in_3), .Cin(FA0_cout), .Sum(S1), .Cout(FA1_cout));
  FullAdder FA2 (.A(in_6), .B(in_5), .Cin(FA1_cout), .Sum(S2), .Cout(FA2_cout));
  FullAdder FA3 (.A(in_8), .B(in_7), .Cin(FA2_cout), .Sum(S3), .Cout(FA3_cout));
  FullAdder FA4 (.A(in_10), .B(in_9), .Cin(FA3_cout), .Sum(S4), .Cout(FA4_cout));
  FullAdder FA5 (.A(in_12), .B(in_11), .Cin(FA4_cout), .Sum(S5), .Cout(FA5_cout));
  FullAdder FA6 (.A(in_14), .B(in_13), .Cin(FA5_cout), .Sum(S6), .Cout(FA6_cout));
  FullAdder FA7 (.A(in_16), .B(in_15), .Cin(FA6_cout), .Sum(S7), .Cout(Cout));
endmodule

module AddSub (
  input  Sub,
  input  A0,
  input  B0,
  input  A1,
  input  B1,
  input  A2,
  input  B2,
  input  A3,
  input  B3,
  input  A4,
  input  B4,
  input  A5,
  input  B5,
  input  A6,
  input  B6,
  input  A7,
  input  B7,
  output S0,
  output S1,
  output S2,
  output S3,
  output S4,
  output S5,
  output S6,
  output S7,
  output Cout
);

  wire xor_1_out, xor_2_out, xor_3_out, xor_4_out, xor_5_out, xor_6_out, xor_7_out, xor_8_out;

  xor xor_1 (xor_1_out, B0, Sub);
  xor xor_2 (xor_2_out, B1, Sub);
  xor xor_3 (xor_3_out, B2, Sub);
  xor xor_4 (xor_4_out, B3, Sub);
  xor xor_5 (xor_5_out, B4, Sub);
  xor xor_6 (xor_6_out, Sub, B5);
  Adder8bit adder8bit_1 (
    .Cin(Sub), .in_1(A0), .in_2(xor_1_out), .in_3(A1), .in_4(xor_2_out), .in_5(A2), .in_6(xor_3_out),
    .in_7(A3), .in_8(xor_4_out), .in_9(A4), .in_10(xor_5_out), .in_11(A5), .in_12(xor_6_out), .in_13(A6),
    .in_14(xor_7_out), .in_15(A7), .in_16(xor_8_out), .S0(S0), .S1(S1), .S2(S2), .S3(S3), .S4(S4), .S5(S5),
    .S6(S6), .S7(S7), .Cout(Cout));
  xor xor_7 (xor_7_out, Sub, B6);
  xor xor_8 (xor_8_out, Sub, B7);
endmodule

module Multiplier (
  input  [7:0] A,
  input  [7:0] B,
  output [7:0] out_3
);

  Multiplier_part multiplier_1 (.a(A), .b(B), .out(out_3), .cin({8{1'b0}}));  // open: cout
endmodule

module Divider (
  input  [7:0] A,
  input  [7:0] B,
  output [7:0] Result,
  output [7:0] Remainder
);

  Divider_part divider_1 (.a(A), .b(B), .out(Result), .upper({8{1'b0}}), .rem(Remainder));
endmodule
