// Logisim project FullAdder.circ as structural Verilog: 1 circuit, main circuit FullAdder
module FullAdder (
  input  A,
  input  B,
  input  Cin,
  output S,
  output Cout
);

  wire and_1_out, and_2_out, xor_1_out;

  // XOR_Gate xor_1 has open pins: out=xor_1_out
  // AND_Gate and_1 has open pins: out=and_1_out
  // XOR_Gate xor_2 has open pins: out=S
  // AND_Gate and_2 has open pins: out=and_2_out
  buf or_1 (Cout, and_2_out);  // OR_Gate
endmodule
